# Fritzing sketch project-setup (saved by Fritzing 0.9.3b)

parts:
  Arduino_Pro_Mini_3_3V_8_Mhz = Arduino Pro Mini v13
  Arduino_Uno = Arduino Uno (Rev3)
  1-RFM69W = RFM69W HopeRF RF 13dBm RF transceiver
  2-RFM69W = RFM69W HopeRF RF 13dBm RF transceiver
  TH1 = TH02 HopeRF RF 13dBm RF transceiver

nets:
  VCC: Arduino_Pro_Mini_3_3V_8_Mhz.VCC, 2-RFM69W.3.3V, TH1.VDD
  N1: Arduino_Pro_Mini_3_3V_8_Mhz.A4, TH1.SDA
  N2: Arduino_Pro_Mini_3_3V_8_Mhz.A5, TH1.SCK
  GND: Arduino_Pro_Mini_3_3V_8_Mhz.GND, 2-RFM69W.GND, TH1.GND
  N3: Arduino_Pro_Mini_3_3V_8_Mhz.D13/SCK, 2-RFM69W.SCK
  N4: Arduino_Pro_Mini_3_3V_8_Mhz.D12/MISO, 2-RFM69W.MISO
  N5: Arduino_Pro_Mini_3_3V_8_Mhz.D11_PWM/MOSI, 2-RFM69W.MOSI
  N6: Arduino_Pro_Mini_3_3V_8_Mhz.D10_PWM/SS, 2-RFM69W.NSS
  N7: Arduino_Pro_Mini_3_3V_8_Mhz.D9_PWM, 2-RFM69W.RESET
  N8: Arduino_Pro_Mini_3_3V_8_Mhz.D2, 2-RFM69W.DIO0
  N9: Arduino_Uno.D10_PWM/SS, 1-RFM69W.NSS
  N10: Arduino_Uno.D11_PWM/MOSI, 1-RFM69W.MOSI
  N11: Arduino_Uno.D12/MISO, 1-RFM69W.MISO
  N12: Arduino_Uno.D13/SCK, 1-RFM69W.SCK
  GND_2: Arduino_Uno.GND, 1-RFM69W.GND
  N13: Arduino_Uno.D2, 1-RFM69W.DIO0
  3V3: Arduino_Uno.3V3, 1-RFM69W.3.3V

custom parts:
  RFM69W HopeRF RF 13dBm RF transceiver: The RFM69W is a highly integrated RF transceiver capable of operation over a wide frequency range, including the 433, 868 and 915 MHz license-free ISM (Industry Scientific and Medical) frequency bands. Its highly integrated architecture allows for a minimum of external components whilst maintaining maximum design flexibility. All major RF communication parameters are programmable and most of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
  TH02 HopeRF RF 13dBm RF transceiver: The TH02 is a digital relative humidity and temperature sensor. This monolithic CMOS IC integrates temperature and humidity sensor elements, an analog-to-digital converter, signal processing, calibration data, and an I2C host interface. The patented use of industry-standard, low-K polymeric dielectrics for sensing humidity enables the construction of a low-power, monolithic CMOS sensor IC with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

// code stored in the sketch: Receiver.ino
/* RFM69 library and code by Felix Rusu - felix@lowpowerlab.com
// Get libraries at: https://github.com/LowPowerLab/
// Make sure you adjust the settings in the configuration section below !!!
// **********************************************************************************
// Copyright Felix Rusu, LowPowerLab.com
// Library and code by Felix Rusu - felix@lowpowerlab.com
// **********************************************************************************
// License
// **********************************************************************************
// This program is free software; you can redistribute it 
// and/or modify it under the terms of the GNU General    
// Public License as published by the Free Software       
// Foundation; either version 3 of the License, or        
// (at your option) any later version.                    
//                                                        
// This program is distributed in the hope that it will   
// be useful, but WITHOUT ANY WARRANTY; without even the  
// implied warranty of MERCHANTABILITY or FITNESS FOR A   
// PARTICULAR PURPOSE. See the GNU General Public        
// License for more details.                              
//                                                        
// You should have received a copy of the GNU General    
// Public License along with this program.
// If not, see <http://www.gnu.org/licenses></http:>.
//                                                        
// Licence can be viewed at                               
// http://www.gnu.org/licenses/gpl-3.0.txt
//
// Please maintain this license information along with authorship
// and copyright notices in any redistribution of this code
// **********************************************************************************/

#include <RFM69.h>    //get it here: https://www.github.com/lowpowerlab/rfm69
#include <SPI.h>

//*********************************************************************************************
// *********** IMPORTANT SETTINGS - YOU MUST CHANGE/ONFIGURE TO FIT YOUR HARDWARE *************
//*********************************************************************************************
#define NETWORKID     100  //the same on all nodes that talk to each other
#define NODEID        1  

//Match frequency to the hardware version of the radio
#define FREQUENCY     RF69_433MHZ
//#define FREQUENCY     RF69_868MHZ
//#define FREQUENCY      RF69_915MHZ
#define ENCRYPTKEY     "7-R|6tITi;JQjw_m" //exactly the same 16 characters/bytes on all nodes!
#define IS_RFM69HCW    false // set to 'true' if you are using an RFM69HCW module

//*********************************************************************************************
#define SERIAL_BAUD   115200

#define RFM69_CS      10
#define RFM69_IRQ     2
#define RFM69_IRQN    0  // Pin 2 is IRQ 0!
#define RFM69_RST     9

#define LED           8  // onboard blinky

int16_t packetnum = 0;  // packet counter, we increment per xmission

RFM69 radio = RFM69(RFM69_CS, RFM69_IRQ, IS_RFM69HCW, RFM69_IRQN);

void setup() {
//  while (!Serial); // wait until serial console is open, remove if not tethered to computer
  Serial.begin(SERIAL_BAUD);

  Serial.println("RFM69W Receiver");
  
  // Hard Reset the RFM module
  pinMode(RFM69_RST, OUTPUT);
  digitalWrite(RFM69_RST, HIGH);
  delay(100);
  digitalWrite(RFM69_RST, LOW);
  delay(100);
  
  // Initialize radio
  radio.initialize(FREQUENCY,NODEID,NETWORKID);
  if (IS_RFM69HCW) {
    radio.setHighPower();    // Only for RFM69HCW & HW!
  }
  radio.setPowerLevel(31); // power output ranges from 0 (5dBm) to 31 (20dBm)
  
  radio.encrypt(ENCRYPTKEY);
  
  pinMode(LED, OUTPUT);

  Serial.print("\nListening at ");
  Serial.print(FREQUENCY==RF69_433MHZ ? 433 : FREQUENCY==RF69_868MHZ ? 868 : 915);
  Serial.println(" MHz");
}

void loop() {
  //check if something was received (could be an interrupt from the radio)
  if (radio.receiveDone())
  {
    //print message received to serial
    Serial.print('[');Serial.print(radio.SENDERID);Serial.print("] ");
    Serial.print((char*)radio.DATA);
    Serial.print("   [RX_RSSI:");Serial.print(radio.RSSI);Serial.println("]");

    //check if received message contains Hello World
    if (strstr((char *)radio.DATA, "Hello World"))
    {
      //check if sender wanted an ACK
      if (radio.ACKRequested())
      {
        radio.sendACK();
        Serial.println(" - ACK sent");
      }
      Blink(LED, 40, 3); //blink LED 3 times, 40ms between blinks
    }  
  }

  radio.receiveDone(); //put radio in RX mode
  Serial.flush(); //make sure all serial data is clocked out before sleeping the MCU
}

void Blink(byte PIN, byte DELAY_MS, byte loops)
{
  for (byte i=0; i<loops; i++)
  {
    digitalWrite(PIN,HIGH);
    delay(DELAY_MS);
    digitalWrite(PIN,LOW);
    delay(DELAY_MS);
  }
}

// code stored in the sketch: TH02.ino
// **********************************************************************************
// Example file reading temperature and humidity from TH02 sensor
// **********************************************************************************
// Creative Commons Attrib Share-Alike License
// You are free to use/extend this library but please abide with the CC-BY-SA license:
// http://creativecommons.org/licenses/by-sa/4.0/
//
// For any explanation see TH02 sensor information at
// http://www.hoperf.com/sensor/app/TH02.htm

// Code based on following datasheet
// http://www.hoperf.com/upload/sensor/TH02_V1.1.pdf 
//
// Written by Charles-Henri Hallard (http://hallard.me)
//
// History : V1.00 2014-07-14 - First release
//           V1.10 2015-04-13 - changed to Wire library instead of I2C
//
// All text above must be included in any redistribution.
//
// **********************************************************************************

#include <arduino.h>
#include <Wire.h>
#include <TH02.h>

// Instantiate TH02 sensor
TH02 th02(TH02_I2C_ADDR);

boolean TH02_found = false;

/* ======================================================================
Function: printhex
Purpose : print hex value in 2 digit format
Input   : value
Output  : 
Comments: 
====================================================================== */
void printhex(uint8_t c)
{
  if (c<16) 
    Serial.print('0');
  Serial.print(c,HEX);
}

/* ======================================================================
Function: i2cScan
Purpose : scan I2C bus
Input   : -
Output  : number of I2C devices seens
Comments: global var TH02_found set to true if found TH02
====================================================================== */
int i2cScan()
{
  byte error, address;
  int nDevices;

  Serial.println("Scanning I2C bus ...");

  nDevices = 0;
  for(address = 1; address < 127; address++ ) 
  {
    // The i2c_scanner uses the return value of
    // the Write.endTransmisstion to see if
    // a device did acknowledge to the address.
    Wire.beginTransmission(address);
    error = Wire.endTransmission();

    if (error == 0)
    {
      Serial.print(F("I2C device found at address 0x"));
      printhex(address);
      
      if (address == 0x40)
      {

        Serial.println(F("-> TH02 !"));
        TH02_found = true;
      }
      else 
        Serial.println(F("-> Unknown device !"));

      nDevices++;
    }
    else if (error==4) 
    {
      Serial.print(F("Unknow error at address 0x"));
      if (address<16) 
        Serial.print('0');
      Serial.println(address,HEX);
    }    
  }
  if (nDevices == 0)
    Serial.println(F("No I2C devices found\n"));
  else
    Serial.println(F("Scan done"));

  return nDevices;
}

/* ======================================================================
Function: setup
Purpose : 
Input   : 
Output  : 
Comments: 
====================================================================== */
void TH02setup()
{
  uint8_t devID;
  uint8_t err;
  uint8_t status;
  uint8_t config;
  
  Serial.begin(115200);
  Serial.println(F("\r\nTH02 Demo"));

  Wire.begin();

  // Loop until we found TH02 module
  while (!TH02_found)
  {
    // scan I2C bus
    i2cScan();

    // We found it ?
    if (TH02_found)
    {
      // TH02 ID 
      err = th02.getId(&devID);

      if (err)
      {
        Serial.print(F("TH02 getId error = 0x"));
        printhex(err);
        Serial.println();
      }
      else
      {
        Serial.print(F("TH02 device ID = 0x"));
        printhex(devID);
        Serial.println();

        if (devID == 0x50)
        {
          Serial.println(F("TH02 device ID match !"));

          if ( (err=th02.getStatus(&status)) != 0)
          {
            Serial.print(F("TH02 Status error = 0x"));
            printhex(err);
          }
          else
          {
            Serial.print(F("TH02 Status = 0x"));
            printhex(status);
          }
          Serial.println();

          if ( (err=th02.getConfig(&config)) != 0)
          {
            Serial.print(F("TH02 Config error = 0x"));
            printhex(err);
          }
          else
          {
            Serial.print(F("TH02 Config = 0x"));
            printhex(config);
          }
          Serial.println();
        }
      }
    }

    // wait until next search
    if (!TH02_found)
    {
      Serial.println(F("Will retry to find TH02 in 5 sec."));
      delay(5000);
    }

  } // While not found
}

/* ======================================================================
Function: loop
Purpose : 
Input   : 
Output  : 
Comments: 
====================================================================== */
void TH02run()
{
  int16_t temp, rh, rh_comp;
  uint8_t duration;
  //uint8_t status;

//  Serial.print(F("Starting Temperature conversion."));
  th02.startTempConv();
  duration = th02.waitEndConversion();
  
/*  if (duration<=TH02_CONVERSION_TIME_OUT)
    Serial.print(F(".done in "));
  else
    Serial.print(F(".timed out "));

  Serial.print(duration);
  Serial.println(F("ms"));
*/    
  // Get temperature calculated and rounded
  temp = th02.getConversionValue();

  if (temp == TH02_UNDEFINED_VALUE)
  {
    Serial.print(F("Error reading value="));
    Serial.println(temp);
  }
  else
  {
//inserted 1 row cj
    th02Trnd=temp/10.0;

/*Display not needed, commented
    // Display unrounded value (raw)
    Serial.print(F("Temperature = "));
    // this call does not do any I2C reading, it use last reading
    Serial.print(th02.getLastRawTemp()/100.0);
    Serial.print(F(" C  =>  "));
    // Display now rounded value returned by 1st call
    Serial.print(temp/10.0);
    Serial.println(F(" C"));
*/
  }
    

//  Serial.print(F("Starting Humidity conversion."));
  
  // Convert humidity
  th02.startRHConv();
  duration = th02.waitEndConversion();
/*
  if (duration<=TH02_CONVERSION_TIME_OUT)
    Serial.print(F(".done in "));
  else
    Serial.print(F(".timed out "));

  Serial.print(duration);
  Serial.println(F("ms"));
*/
  // Get temperature calculated and rounded with no compensation
  rh = th02.getConversionValue();

  if (rh == TH02_UNDEFINED_VALUE)
  {
    Serial.print(F("Error reading value="));
    Serial.println(rh);
  }
  else
  { 
//inserted 1 row (cj)
    th02Hrnd=th02.getConpensatedRH(true)/10.0;
/*Display not needed, commented (cj)
    // Now display last reading with unrounded value 
    // this call does not do any I2C reading, it use last reading
    Serial.print(F("Raw Humidity = "));
    Serial.print(th02.getLastRawRH()/100.0);
    Serial.print(F("%  => Compensated "));
    Serial.print(th02.getConpensatedRH(false)/100.0);
    Serial.print(F("%  Rounded  "));
    Serial.print(th02Hrnd);
    Serial.print(th02.getConpensatedRH(true)/10.0);
    Serial.println(F("%"));
*/
  }
/*
  Serial.println(F("Now waiting 10 sec before next conversion."));
  delay(10000);
*/
}

// code stored in the sketch: Transmitter.ino
/* RFM69 library and code by Felix Rusu - felix@lowpowerlab.com
// Get libraries at: https://github.com/LowPowerLab/
// Make sure you adjust the settings in the configuration section below !!!
// **********************************************************************************
// Copyright Felix Rusu, LowPowerLab.com
// Library and code by Felix Rusu - felix@lowpowerlab.com
// **********************************************************************************
// License
// **********************************************************************************
// This program is free software; you can redistribute it 
// and/or modify it under the terms of the GNU General    
// Public License as published by the Free Software       
// Foundation; either version 3 of the License, or        
// (at your option) any later version.                    
//                                                        
// This program is distributed in the hope that it will   
// be useful, but WITHOUT ANY WARRANTY; without even the  
// implied warranty of MERCHANTABILITY or FITNESS FOR A   
// PARTICULAR PURPOSE. See the GNU General Public        
// License for more details.                              
//                                                        
// You should have received a copy of the GNU General    
// Public License along with this program.
// If not, see <http://www.gnu.org/licenses></http:>.
//                                                        
// Licence can be viewed at                               
// http://www.gnu.org/licenses/gpl-3.0.txt
//
// Please maintain this license information along with authorship
// and copyright notices in any redistribution of this code
// **********************************************************************************/

#include <RFM69.h>    //get it here: https://www.github.com/lowpowerlab/rfm69
#include <SPI.h>

//*********************************************************************************************
// *********** IMPORTANT SETTINGS - YOU MUST CHANGE/ONFIGURE TO FIT YOUR HARDWARE *************
//*********************************************************************************************
#define NETWORKID     100  //the same on all nodes that talk to each other
#define NODEID        1  

//Match frequency to the hardware version of the radio
#define FREQUENCY     RF69_433MHZ
//#define FREQUENCY     RF69_868MHZ
//#define FREQUENCY      RF69_915MHZ
#define ENCRYPTKEY     "7-R|6tITi;JQjw_m" //exactly the same 16 characters/bytes on all nodes!
#define IS_RFM69HCW    false // set to 'true' if you are using an RFM69HCW module

//*********************************************************************************************
#define SERIAL_BAUD   115200

#define RFM69_CS      10
#define RFM69_IRQ     2
#define RFM69_IRQN    0  // Pin 2 is IRQ 0!
#define RFM69_RST     9

#define LED           8  // onboard blinky

int16_t packetnum = 0;  // packet counter, we increment per xmission

RFM69 radio = RFM69(RFM69_CS, RFM69_IRQ, IS_RFM69HCW, RFM69_IRQN);

void setup() {
//  while (!Serial); // wait until serial console is open, remove if not tethered to computer
  Serial.begin(SERIAL_BAUD);

  Serial.println("RFM69W Receiver");
  
  // Hard Reset the RFM module
  pinMode(RFM69_RST, OUTPUT);
  digitalWrite(RFM69_RST, HIGH);
  delay(100);
  digitalWrite(RFM69_RST, LOW);
  delay(100);
  
  // Initialize radio
  radio.initialize(FREQUENCY,NODEID,NETWORKID);
  if (IS_RFM69HCW) {
    radio.setHighPower();    // Only for RFM69HCW & HW!
  }
  radio.setPowerLevel(31); // power output ranges from 0 (5dBm) to 31 (20dBm)
  
  radio.encrypt(ENCRYPTKEY);
  
  pinMode(LED, OUTPUT);

  Serial.print("\nListening at ");
  Serial.print(FREQUENCY==RF69_433MHZ ? 433 : FREQUENCY==RF69_868MHZ ? 868 : 915);
  Serial.println(" MHz");
}

void loop() {
  //check if something was received (could be an interrupt from the radio)
  if (radio.receiveDone())
  {
    //print message received to serial
    Serial.print('[');Serial.print(radio.SENDERID);Serial.print("] ");
    Serial.print((char*)radio.DATA);
    Serial.print("   [RX_RSSI:");Serial.print(radio.RSSI);Serial.println("]");

    //check if received message contains Hello World
    if (strstr((char *)radio.DATA, "Hello World"))
    {
      //check if sender wanted an ACK
      if (radio.ACKRequested())
      {
        radio.sendACK();
        Serial.println(" - ACK sent");
      }
      Blink(LED, 40, 3); //blink LED 3 times, 40ms between blinks
    }  
  }

  radio.receiveDone(); //put radio in RX mode
  Serial.flush(); //make sure all serial data is clocked out before sleeping the MCU
}

void Blink(byte PIN, byte DELAY_MS, byte loops)
{
  for (byte i=0; i<loops; i++)
  {
    digitalWrite(PIN,HIGH);
    delay(DELAY_MS);
    digitalWrite(PIN,LOW);
    delay(DELAY_MS);
  }
}
